# Fritzing sketch ADKeypad (saved by Fritzing 0.9.4)
circuit board: 8.47cm x 5.64cm
breadboards: 1

parts:
  R_pullup = Resistor [tolerance=±5% resistance=220k package=THT]
  R_row2 = Resistor [tolerance=±5% resistance=15k package=THT]
  R_row0 = Resistor [tolerance=±1% resistance=22k package=THT]
  R_row1 = Resistor [tolerance=±1% resistance=15k package=THT]
  R_col1 = Resistor [tolerance=±1% resistance=68k package=THT]
  R_col0 = Resistor [tolerance=±1% resistance=68k package=THT]
  KeyPad = male pin header, 7 pins [form="♂ (male)"]
  Part1 = Arduino Uno (Rev3)

nets:
  N1: R_pullup.Pin_0, Part1.3V3
  N2: R_pullup.Pin_1, R_col0.Pin_0, KeyPad.pin3, Part1.A0
  N3: R_row2.Pin_0, KeyPad.pin4, Part1.GND
  N4: R_row2.Pin_1, R_row1.Pin_0, KeyPad.pin5
  N5: R_row0.Pin_0, R_row1.Pin_1, KeyPad.pin6
  N6: R_row0.Pin_1, KeyPad.pin7
  N7: R_col1.Pin_0, R_col0.Pin_1, KeyPad.pin2
  N8: R_col1.Pin_1, KeyPad.pin1
